# Fritzing sketch memorygame (saved by Fritzing 0.9.3b)
breadboards: 1

parts:
  Raspberry_Pi_1 = Raspberry Pi 3 [part_number=RPI-3-V1.2]
  LED1 = LED - 5mm [color="Red (633nm)" package="5 mm [THT]"]
  LED2 = LED - 5mm [color="Yellow (595nm)" package="5 mm [THT]"]
  LED3 = LED - 5mm [color="Green (555nm)" package="5 mm [THT]"]
  LED4 = LED - 5mm [color="Blue (430nm)" package="5 mm [THT]"]
  R1 = Resistor [tolerance=±5% resistance=220 package=THT]
  R2 = Resistor [tolerance=±5% resistance=220 package=THT]
  R3 = Resistor [tolerance=±5% resistance=220 package=THT]
  R4 = Resistor [tolerance=±5% resistance=220 package=THT]
  S1 = Pushbutton [package="[THT]"]
  S2 = Pushbutton [package="[THT]"]
  S3 = Pushbutton [package="[THT]"]
  S4 = Pushbutton [package="[THT]"]

nets:
  N1: Raspberry_Pi_1.GPIO2, LED1.anode
  N2: Raspberry_Pi_1.GPIO3, LED2.anode
  N3: Raspberry_Pi_1.GPIO4, LED3.anode
  N4: Raspberry_Pi_1.GPIO17, LED4.anode
  N5: Raspberry_Pi_1.GND, R1.Pin_1, R2.Pin_1, R3.Pin_1, R4.Pin_1, S1.Pin_3, S1.Pin_4, S2.Pin_3, S2.Pin_4, S3.Pin_3, S3.Pin_4, S4.Pin_3, S4.Pin_4
  N6: Raspberry_Pi_1.GPIO23, S4.Pin_1, S4.Pin_2
  N7: Raspberry_Pi_1.GPIO18, S3.Pin_1, S3.Pin_2
  N8: Raspberry_Pi_1.GPIO15, S2.Pin_1, S2.Pin_2
  N9: Raspberry_Pi_1.GPIO14, S1.Pin_1, S1.Pin_2
  N10: LED1.cathode, R1.Pin_0
  N11: LED2.cathode, R2.Pin_0
  N12: LED3.cathode, R3.Pin_0
  N13: LED4.cathode, R4.Pin_0
